// Digital circuit MICO XII.dig as structural Verilog
module MICO_XII (
  input  clk
);

  wire [9:0] MC_out;
  wire [15:0] add_1_s, banco_de_registradores_1_p6, IP_q, multiplexer_1_out;
  wire [15:1] undriven;
  wire [31:0] banco_de_registradores_1_p7, bitextender_1_out, MI_d, multiplexer_2_out;

  Add #(.Bits(16)) add_1 (.a(IP_q), .b({undriven, 1'b1}), .c_i(1'b0), .s(add_1_s));  // open: c_o
  Multiplexer #(.Selector_Bits(2), .Bits(16)) multiplexer_1 (
    .sel(MC_out[8:7]), .in_0(add_1_s), .in_2(banco_de_registradores_1_p6), .in_3(IP_q),
    .out(multiplexer_1_out));  // open: in_1
  Register #(.Bits(16)) IP (.D(multiplexer_1_out), .C(clk), .en(1'b1), .Q(IP_q));
  ROM #(.Bits(32)) MI (.A(IP_q[1:0]), .D(MI_d));  // open: sel
  // Banco_de_registradores banco_de_registradores_1: pin names not known; wires that end beside it: clk, MI_d[7:4], MI_d[11:8], MI_d[15:12], MC_out[6], banco_de_registradores_1_p6, banco_de_registradores_1_p7
  BitExtender #(.inputBits(16), .outputBits(32)) bitextender_1 (.in(MI_d[31:16]), .out(bitextender_1_out));
  LookUpTable #(.Bits(10)) MC (.in0(MI_d[0]), .in1(MI_d[1]), .in2(MI_d[2]), .in3(MI_d[3]), .out(MC_out));
  Multiplexer #(.Bits(32)) multiplexer_2 (
    .sel(MC_out[5]), .in_0(banco_de_registradores_1_p7), .in_1(bitextender_1_out), .out(multiplexer_2_out));
  // ULA ula_1: pin names not known; wires that end beside it: banco_de_registradores_1_p6, multiplexer_2_out, MC_out[2:0]
  Seven_Seg #(.commonConnectionType("anode")) seven_seg_1 (.a(MC_out[9]));  // open: b, c, d, e, f, g, dp
  RAMDualPort #(.AddrBits(24), .Bits(32)) ramdualport_1 (.str(MC_out[4]), .ld(MC_out[3]));  // open: A, Din, C, D
  // Pins of 2 and 16 bits meet at IP_q
  // Pins of 1 and 16 bits meet at {undriven, 1'b1}

  // Notes on the sheet:
  //   contents of MC (hex, n*v repeats v):
  //   40,41,42,43,44,45,46,47,60,68,70,200,a0,140,67
endmodule
