// Digital circuit PC.dig as structural Verilog
module PC (
  input  Clock,
  input  [31:0] Entrada_mult,
  input  [31:0] seletor_mult,
  output [31:0] IP
);

  wire [31:0] Incrementa_s, multiplexer_1_out;

  Add #(.Bits(32)) Incrementa (.a(IP), .b(32'h4), .s(Incrementa_s));  // open: c_i, c_o
  Multiplexer #(.Bits(32)) multiplexer_1 (
    .sel(seletor_mult[0]), .in_0(Incrementa_s), .in_1(Entrada_mult), .out(multiplexer_1_out));
  Register #(.Bits(32)) register_1 (.D(multiplexer_1_out), .C(Clock), .Q(IP));  // open: en
  // Pins of 1 and 32 bits meet at seletor_mult
endmodule
