// Digital circuit Banco_de_registradores.dig as structural Verilog
module Banco_de_registradores (
  input  CLOCK,
  input  [3:0] A,
  input  [3:0] B,
  input  [3:0] c,
  input  we,
  input  [31:0] Dado,
  output [31:0] saida_A,
  output [31:0] saida_B
);

  wire e0, e1, e2, e3, e4, e5, e6, e7, e8, e9, e10, e11, e12, e13, e14, e15;
  wire [31:0] s0, s1, s2, s3, s4, s5, s6, s7, s8, s9, s10, s11, s12, s13, s14, s15;

  Register register_1 (.D(Dado[0]), .C(CLOCK), .en(e0), .Q(s0[0]));
  Register register_2 (.D(Dado[0]), .C(CLOCK), .en(e1), .Q(s1[0]));
  Register register_3 (.D(Dado[0]), .C(CLOCK), .en(e2), .Q(s2[0]));
  Register register_4 (.D(Dado[0]), .C(CLOCK), .en(e3), .Q(s3[0]));
  Multiplexer #(.Selector_Bits(4), .Bits(32)) multiplexer_1 (
    .sel(A), .in_0(s0), .in_1(s1), .in_2(s2), .in_3(s3), .in_4(s4), .in_5(s5), .in_6(s6), .in_7(s7),
    .in_8(s8), .in_9(s9), .in_10(s10), .in_11(s11), .in_12(s12), .in_13(s13), .in_14(s14), .in_15(s15),
    .out(saida_A));
  Register register_5 (.D(Dado[0]), .C(CLOCK), .en(e4), .Q(s4[0]));
  Register register_6 (.D(Dado[0]), .C(CLOCK), .en(e5), .Q(s5[0]));
  Register register_7 (.D(Dado[0]), .C(CLOCK), .en(e6), .Q(s6[0]));
  Register register_8 (.D(Dado[0]), .C(CLOCK), .en(e7), .Q(s7[0]));
  Multiplexer #(.Selector_Bits(4), .Bits(32)) multiplexer_2 (
    .sel(B), .in_0(s0), .in_1(s1), .in_2(s2), .in_3(s3), .in_4(s4), .in_5(s5), .in_6(s6), .in_7(s7),
    .in_8(s8), .in_9(s9), .in_10(s10), .in_11(s11), .in_12(s12), .in_13(s13), .in_14(s14), .in_15(s15),
    .out(saida_B));
  Register register_9 (.D(Dado[0]), .C(CLOCK), .en(e8), .Q(s8[0]));
  Register register_10 (.D(Dado[0]), .C(CLOCK), .en(e9), .Q(s9[0]));
  Register register_11 (.D(Dado[0]), .C(CLOCK), .en(e10), .Q(s10[0]));
  Register register_12 (.D(Dado[0]), .C(CLOCK), .en(e11), .Q(s11[0]));
  Demultiplexer #(.Selector_Bits(4)) demultiplexer_1 (
    .sel(c), .in(we), .out_0(e0), .out_1(e1), .out_2(e2), .out_3(e3), .out_4(e4), .out_5(e5), .out_6(e6),
    .out_7(e7), .out_8(e8), .out_9(e9), .out_10(e10), .out_11(e11), .out_12(e12), .out_13(e13), .out_14(e14),
    .out_15(e15));
  Register register_13 (.D(Dado[0]), .C(CLOCK), .en(e12), .Q(s12[0]));
  Register register_14 (.D(Dado[0]), .C(CLOCK), .en(e13), .Q(s13[0]));
  Register register_15 (.D(Dado[0]), .C(CLOCK), .en(e14), .Q(s14[0]));
  Register register_16 (.D(Dado[0]), .C(CLOCK), .en(e15), .Q(s15[0]));
  // Pins of 1 and 32 bits meet at Dado
  // Pins of 1 and 32 bits meet at s8
  // Pins of 1 and 32 bits meet at s9
  // Pins of 1 and 32 bits meet at s10
  // Pins of 1 and 32 bits meet at s11
  // Pins of 1 and 32 bits meet at s12
  // Pins of 1 and 32 bits meet at s13
  // Pins of 1 and 32 bits meet at s14
  // Pins of 1 and 32 bits meet at s15
  // Pins of 1 and 32 bits meet at s0
  // Pins of 1 and 32 bits meet at s1
  // Pins of 1 and 32 bits meet at s2

  // Other names for the same wires on the sheet: C_t[31:0] = Dado; clk = CLOCK
endmodule
