// Digital circuit MICO XII.dig as structural Verilog
module MICO_XII (
  input  clk
);

  wire banco_de_registradores_1_p8;
  wire [1:0] register_1_q;
  wire [15:0] add_1_s, banco_de_registradores_1_p6, multiplexer_1_out;
  wire [31:0] banco_de_registradores_1_p7, bitextender_1_out, multiplexer_2_out, rom_1_d;

  Add add_1 (.a(register_1_q[0]), .b(1'b1), .s(add_1_s[0]));  // open: c_i, c_o
  Multiplexer #(.Selector_Bits(2), .Bits(16)) multiplexer_1 (
    .in_0(add_1_s), .in_2(banco_de_registradores_1_p6), .out(multiplexer_1_out));  // open: sel, in_1, in_3
  Register register_1 (.D(multiplexer_1_out[0]), .C(clk), .en(1'b1), .Q(register_1_q[0]));
  ROM #(.Bits(32)) rom_1 (.A(register_1_q), .D(rom_1_d));  // open: sel
  // Banco_de_registradores banco_de_registradores_1: pin names not known; wires that end beside it: clk, rom_1_d[7:4], rom_1_d[11:8], rom_1_d[15:12], rom_1_d[3:0], banco_de_registradores_1_p6, banco_de_registradores_1_p7, banco_de_registradores_1_p8
  BitExtender #(.inputBits(16), .outputBits(32)) bitextender_1 (.in(rom_1_d[31:16]), .out(bitextender_1_out));
  Multiplexer #(.Bits(32)) multiplexer_2 (
    .sel(banco_de_registradores_1_p8), .in_0(banco_de_registradores_1_p7), .in_1(bitextender_1_out),
    .out(multiplexer_2_out));
  // ULA ula_1: pin names not known; wires that end beside it: banco_de_registradores_1_p6, multiplexer_2_out
  RAMDualPort #(.AddrBits(24), .Bits(32)) ramdualport_1 ();  // open: A, Din, str, C, ld, D
  Seven_Seg seven_seg_1 ();  // open: a, b, c, d, e, f, g, dp
  // Pins of 1 and 2 bits meet at register_1_q
  // Pins of 1 and 16 bits meet at add_1_s
  // Pins of 1 and 16 bits meet at multiplexer_1_out
endmodule
