// Digital circuit MIPS.dig as structural Verilog
module MIPS (
  input  clk
);

  wire add_1_c_o, AluSrc, and_1_out, Branch, Enable, Incrementa_c_o, notconnected_1_out, notconnected_2_out,
       notconnected_3_out, notconnected_4_out, notconnected_5_out, notconnected_6_out, notconnected_7_out,
       notconnected_8_out, ula_1_zero, we;
  wire [2:0] AluOP;
  wire [3:0] and_2_out, and_2_out_3, and_2_out_4, and_2_out_5, and_2_out_6, and_2_out_7, and_2_out_8;
  wire [7:4] and_2_out_2;
  wire [15:0] MI_d, MI_d_2;
  wire [23:0] add_1_s, bitextender_1_out, Incrementa_s, IP_q, multiplexer_1_out;
  wire [31:0] banco_de_registradores_1_s_a, banco_de_registradores_1_s_b, bitextender_2_out,
       bitextender_3_out, multiplexer_2_out, ula_1_s;

  Add #(.Bits(24)) Incrementa (.a(IP_q), .b(24'h1), .c_i(1'b0), .s(Incrementa_s), .c_o(Incrementa_c_o));
  Add #(.Bits(24)) add_1 (.a(Incrementa_s), .b(bitextender_1_out), .c_i(1'b0), .s(add_1_s), .c_o(add_1_c_o));
  BitExtender #(.inputBits(16), .outputBits(24)) bitextender_1 (.in(MI_d_2), .out(bitextender_1_out));
  Multiplexer #(.Bits(24)) multiplexer_1 (
    .sel(and_1_out), .in_0(Incrementa_s), .in_1(add_1_s), .out(multiplexer_1_out));
  and and_1 (and_1_out, ula_1_zero, Branch);
  Register #(.Bits(24)) IP (.D(multiplexer_1_out), .C(clk), .en(1'b1), .Q(IP_q));
  Seven_Seg_Hex seven_seg_hex_1 (.d(and_2_out_8), .dp(notconnected_1_out));
  ROM #(.AddrBits(24), .Bits(32)) MI (.A(IP_q), .sel(1'b1), .D({MI_d_2, MI_d}));
  Seven_Seg_Hex seven_seg_hex_2 (.d(and_2_out_7), .dp(notconnected_2_out));
  // NotConnected on notconnected_1_out
  // NotConnected on notconnected_2_out
  Seven_Seg_Hex seven_seg_hex_3 (.d(and_2_out_6), .dp(notconnected_3_out));
  // NotConnected on notconnected_3_out
  Seven_Seg_Hex seven_seg_hex_4 (.d(and_2_out_5), .dp(notconnected_4_out));
  Seven_Seg_Hex seven_seg_hex_5 (.d(and_2_out_4), .dp(notconnected_5_out));
  // NotConnected on notconnected_4_out
  BitExtender #(.inputBits(1), .outputBits(32)) bitextender_2 (.in(Enable), .out(bitextender_2_out));
  Banco_de_registradores banco_de_registradores_1 (
    .A(MI_d[7:4]), .B(MI_d[11:8]), .c(MI_d[15:12]), .we(we), .C_2(ula_1_s), .clk(clk),
    .s_a(banco_de_registradores_1_s_a), .s_b(banco_de_registradores_1_s_b));
  Seven_Seg_Hex seven_seg_hex_6 (.d(and_2_out_3), .dp(notconnected_6_out));
  // NotConnected on notconnected_5_out
  BitExtender #(.inputBits(16), .outputBits(32)) bitextender_3 (.in(MI_d_2), .out(bitextender_3_out));
  // NotConnected on notconnected_6_out
  assign {and_2_out_8, and_2_out_7, and_2_out_6, and_2_out_5, and_2_out_4, and_2_out_3, and_2_out_2, and_2_out} = bitextender_2_out & banco_de_registradores_1_s_a;  // And and_2, 32 bits wide
  Multiplexer #(.Bits(32)) multiplexer_2 (
    .sel(AluSrc), .in_0(banco_de_registradores_1_s_b), .in_1(bitextender_3_out), .out(multiplexer_2_out));
  Seven_Seg_Hex seven_seg_hex_7 (.d(and_2_out_2), .dp(notconnected_7_out));
  // NotConnected on notconnected_7_out
  Seven_Seg_Hex seven_seg_hex_8 (.d(and_2_out), .dp(notconnected_8_out));
  ULA ula_1 (.A(banco_de_registradores_1_s_a), .B(multiplexer_2_out), .FUN(AluOP), .S(ula_1_s), .Zero(ula_1_zero));
  // NotConnected on notconnected_8_out
  ROM #(.AddrBits(4), .Bits(7)) MC (.A(MI_d[3:0]), .sel(1'b1), .D({we, AluSrc, AluOP, Enable, Branch}));
  // also tied to GND on the sheet: {add_1_c_o, Incrementa_c_o}

  // Notes on the sheet:
  //   contents of MI (hex, n*v repeats v):
  //   a0000211,70000311,21000411,511,711,15663,efff061c,9754,eb42,9f42
  //   ,10000b69,dfff00b,1c6d,e
  //   contents of MC (hex, n*v repeats v):
  //   0,61,44,48,4c,50,54,58,5c,64,68,21,61,43,1
endmodule
