// Digital circuit SHIFTERLEFT.dig as structural Verilog
module SHIFTERLEFT (
  input  [31:0] A,
  input  [31:0] B,
  output [31:0] S
);

  wire [31:0] shifter1b_1_s, shifter2b_1_s, shifter4b_1_s, shifter8b_1_s;

  shifter1b shifter1b_1 (.A(A), .B(B[0]), .S(shifter1b_1_s));
  shifter2b shifter2b_1 (.A(shifter1b_1_s), .B(B[1]), .S(shifter2b_1_s));
  shifter4b shifter4b_1 (.A(shifter2b_1_s), .B(B[2]), .S(shifter4b_1_s));
  shifter8b shifter8b_1 (.A(shifter4b_1_s), .B(B[3]), .S(shifter8b_1_s));
  shifter16b shifter16b_1 (.A(shifter8b_1_s), .B(B[4]), .S(S));
endmodule
