// Digital circuit SOMADOR.dig as structural Verilog
module SOMADOR (
  input  [31:0] A,
  input  [31:0] B,
  output [31:0] S
);

  wire S1_c_o, S2_c_o, S3_c_o, S4_c_o, S5_c_o, S6_c_o, S7_c_o, S8_c_o;

  Add #(.Bits(4)) S1 (.a(A[3:0]), .b(B[3:0]), .c_i(1'b0), .s(S[3:0]), .c_o(S1_c_o));
  Add #(.Bits(4)) S2 (.a(A[7:4]), .b(B[7:4]), .c_i(S1_c_o), .s(S[7:4]), .c_o(S2_c_o));
  Add #(.Bits(4)) S3 (.a(A[11:8]), .b(B[11:8]), .c_i(S2_c_o), .s(S[11:8]), .c_o(S3_c_o));
  Add #(.Bits(4)) S4 (.a(A[15:12]), .b(B[15:12]), .c_i(S3_c_o), .s(S[15:12]), .c_o(S4_c_o));
  Add #(.Bits(4)) S5 (.a(A[19:16]), .b(B[19:16]), .c_i(S4_c_o), .s(S[19:16]), .c_o(S5_c_o));
  Add #(.Bits(4)) S6 (.a(A[23:20]), .b(B[23:20]), .c_i(S5_c_o), .s(S[23:20]), .c_o(S6_c_o));
  Add #(.Bits(4)) S7 (.a(A[27:24]), .b(B[27:24]), .c_i(S6_c_o), .s(S[27:24]), .c_o(S7_c_o));
  Add #(.Bits(4)) S8 (.a(A[31:28]), .b(B[31:28]), .c_i(S7_c_o), .s(S[31:28]), .c_o(S8_c_o));
  // also tied to GND on the sheet: S8_c_o

  // Other names for the same wires on the sheet: s1A[3:0] = A[3:0]; s2A[3:0] = A[7:4]; s3A[3:0] = A[11:8];
  //   s4A[3:0] = A[15:12]; s5A[3:0] = A[19:16]; s6A[3:0] = A[23:20]; s7A[3:0] = A[27:24]; s8A[3:0] = A[31:28];
  //   s1B[3:0] = B[3:0]; s2B[3:0] = B[7:4]; s3B[3:0] = B[11:8]; s4B[3:0] = B[15:12]; s5B[3:0] = B[19:16];
  //   s6B[3:0] = B[23:20]; s7B[3:0] = B[27:24]; s8B[3:0] = B[31:28]; SS1[3:0] = S[3:0]; SS2[3:0] = S[7:4];
  //   SS3[3:0] = S[11:8]; SS4[3:0] = S[15:12]; SS5[3:0] = S[19:16]; SS6[3:0] = S[23:20]; SS7[3:0] = S[27:24];
  //   SS8[3:0] = S[31:28]
endmodule
