// Digital circuit ULA.dig as structural Verilog
module ULA (
  input  [31:0] A,
  input  [31:0] B,
  input  [2:0] FUN,
  output [31:0] S,
  output Zero
);

  wire [31:0] and_1_out, not_1_out, or_1_out, shifterleft_1_s, somador_1_s, \Subtração_s , xor_1_out;
  wire [63:0] mul_1_mul;

  assign not_1_out = ~B;  // Not not_1, 32 bits wide
  SOMADOR somador_1 (.A(A), .B(B), .S(somador_1_s));
  SOMADOR \Subtração  (.A(A), .B(not_1_out), .S(\Subtração_s ));
  Mul #(.Bits(32)) mul_1 (.a(A), .b(B), .mul(mul_1_mul));
  assign and_1_out = A & B;  // And and_1, 32 bits wide
  assign or_1_out = A | B;  // Or or_1, 32 bits wide
  assign xor_1_out = A ^ B;  // XOr xor_1, 32 bits wide
  SHIFTERLEFT shifterleft_1 (.A(A), .B(B), .S(shifterleft_1_s));
  Multiplexer #(.Selector_Bits(3), .Bits(32)) multiplexer_1 (
    .sel(FUN), .in_0(somador_1_s), .in_1(\Subtração_s ), .in_2(mul_1_mul[31:0]), .in_3(and_1_out),
    .in_4(or_1_out), .in_5(xor_1_out), .in_6(shifterleft_1_s), .in_7({32{1'b0}}), .out(S));
  verifica_zero verifica_zero_1 (.En(S), .S(Zero));
endmodule
