// Digital circuit verifica_zero.dig as structural Verilog
module verifica_zero (
  input  [31:0] En,
  output S
);

  nor nor_1 (S, En[0], En[1], En[2], En[3], En[4], En[5], En[6], En[7], En[8], En[9], En[10], En[11], En[12], En[13], En[14], En[15], En[16], En[17], En[18], En[19], En[20], En[21], En[22], En[23], En[24], En[25], En[26], En[27], En[28], En[29], En[30], En[31]);
endmodule
