// Digital circuit ULA.dig as structural Verilog
module ULA (
  input  [31:0] A,
  input  [31:0] B,
  input  [3:0] FUN,
  output [31:0] R
);

  wire [31:0] add_1_s, and_1_out, comparator_1_lt, not_1_out, or_1_out, sub_1_s, xor_1_out;
  wire [63:0] mul_1_mul;

  Add #(.Bits(32)) add_1 (.a(A), .b(B), .c_i(1'b0), .s(add_1_s));  // open: c_o
  Sub #(.Bits(32)) sub_1 (.a(A), .b(B), .c_i(1'b0), .s(sub_1_s));  // open: c_o
  Mul #(.Bits(32)) mul_1 (.a(A), .b(B), .mul(mul_1_mul));
  assign and_1_out = A & B;  // And and_1, 32 bits wide
  assign or_1_out = A | B;  // Or or_1, 32 bits wide
  assign xor_1_out = A ^ B;  // XOr xor_1, 32 bits wide
  Comparator #(.Bits(32)) comparator_1 (.a(A), .b(B), .lt(comparator_1_lt[0]));  // open: gt, eq
  assign not_1_out = ~A;  // Not not_1, 32 bits wide
  Multiplexer #(.Selector_Bits(3), .Bits(32)) multiplexer_1 (
    .sel(FUN[2:0]), .in_0(add_1_s), .in_1(sub_1_s), .in_2(mul_1_mul[31:0]), .in_3(and_1_out),
    .in_4(or_1_out), .in_5(xor_1_out), .in_6(comparator_1_lt), .in_7(not_1_out), .out(R));
  // Pins of 3 and 4 bits meet at FUN
  // Pins of 32 and 64 bits meet at mul_1_mul
  // Pins of 1 and 32 bits meet at comparator_1_lt
  // Pins of 1 and 32 bits meet at {32{1'b0}}
  // Pins of 1 and 32 bits meet at {32{1'b0}}
endmodule
