// Digital circuit Branch.dig as structural Verilog
module Branch (
  input  zero,
  input  IP,
  input  WE,
  output S
);

  wire and_1_out;

  and and_1 (and_1_out, IP, WE);
  Multiplexer multiplexer_1 (.sel(and_1_out), .in_0(IP), .in_1(zero), .out(S));
endmodule
