// Digital circuit IP.dig as structural Verilog
module IP (
  input  [23:0] A,
  input  Clock,
  output [23:0] S
);

  Register #(.Bits(24)) register_1 (.D(A), .C(Clock), .en(1'b1), .Q(S));
endmodule
