// Digital circuit Registrador.dig as structural Verilog
module Registrador (
  input  [3:0] c,
  input  WE,
  input  clock,
  input  [3:0] b,
  input  [3:0] a,
  input  [31:0] C_2,
  output [31:0] A_2,
  output [31:0] B_2
);

  wire w0, w1, w2, w3, w4, w5, w6, w7, w8, w9, w10, w11, w12, w13, w14, w15;
  wire [31:0] reg0, reg1, reg2, reg3, reg4, reg5, reg6, reg7, reg8, reg9, reg10, reg11, reg12, reg13, reg14,
       reg15;

  Demultiplexer #(.Selector_Bits(4)) demultiplexer_1 (
    .sel(c), .in(WE), .out_0(w0), .out_1(w1), .out_2(w2), .out_3(w3), .out_4(w4), .out_5(w5), .out_6(w6),
    .out_7(w7), .out_8(w8), .out_9(w9), .out_10(w10), .out_11(w11), .out_12(w12), .out_13(w13), .out_14(w14),
    .out_15(w15));
  Register #(.Bits(32)) register_1 (.D(C_2), .C(clock), .en(w0), .Q(reg0));
  Register #(.Bits(32)) register_2 (.D(C_2), .C(clock), .en(w1), .Q(reg1));
  Register #(.Bits(32)) register_3 (.D(C_2), .C(clock), .en(w2), .Q(reg2));
  Register #(.Bits(32)) register_4 (.D(C_2), .C(clock), .en(w3), .Q(reg3));
  Register #(.Bits(32)) register_5 (.D(C_2), .C(clock), .en(w4), .Q(reg4));
  Register #(.Bits(32)) register_6 (.D(C_2), .C(clock), .en(w5), .Q(reg5));
  Register #(.Bits(32)) register_7 (.D(C_2), .C(clock), .en(w6), .Q(reg6));
  Register #(.Bits(32)) register_8 (.D(C_2), .C(clock), .en(w7), .Q(reg7));
  Register #(.Bits(32)) register_9 (.D(C_2), .C(clock), .en(w8), .Q(reg8));
  Register #(.Bits(32)) register_10 (.D(C_2), .C(clock), .en(w9), .Q(reg9));
  Register #(.Bits(32)) register_11 (.D(C_2), .C(clock), .en(w10), .Q(reg10));
  Register #(.Bits(32)) register_12 (.D(C_2), .C(clock), .en(w11), .Q(reg11));
  Register #(.Bits(32)) register_13 (.D(C_2), .C(clock), .en(w12), .Q(reg12));
  Register #(.Bits(32)) register_14 (.D(C_2), .C(clock), .en(w13), .Q(reg13));
  Register #(.Bits(32)) register_15 (.D(C_2), .C(clock), .en(w14), .Q(reg14));
  Register #(.Bits(32)) register_16 (.D(C_2), .C(clock), .en(w15), .Q(reg15));
  Multiplexer #(.Selector_Bits(4), .Bits(32)) multiplexer_1 (
    .sel(a), .in_0(reg0), .in_1(reg1), .in_2(reg2), .in_3(reg3), .in_4(reg4), .in_5(reg5), .in_6(reg6),
    .in_7(reg7), .in_8(reg8), .in_9(reg9), .in_10(reg10), .in_11(reg11), .in_12(reg12), .in_13(reg13),
    .in_14(reg14), .in_15(reg15), .out(A_2));
  Multiplexer #(.Selector_Bits(4), .Bits(32)) multiplexer_2 (
    .sel(b), .in_0(reg0), .in_1(reg1), .in_2(reg2), .in_3(reg3), .in_4(reg4), .in_5(reg5), .in_6(reg6),
    .in_7(reg7), .in_8(reg8), .in_9(reg9), .in_10(reg10), .in_11(reg11), .in_12(reg12), .in_13(reg13),
    .in_14(reg14), .in_15(reg15), .out(B_2));

  // Other names for the same wires on the sheet: C_t[31:0] = C_2
endmodule
