// Digital circuit SignedExtesion24bits.dig as structural Verilog
module SignedExtesion24bits (
  input  [15:0] \const ,
  output [23:0] S
);

  Multiplexer #(.Bits(8)) multiplexer_1 (.sel(\const [15]), .in_0({8{1'b0}}), .in_1(8'h1), .out(S[23:16]));

  assign S[15:0] = \const ;
endmodule
