// Digital circuit ip.dig as structural Verilog
module ip (
  input  [23:0] A,
  input  [23:0] B,
  output [23:0] S
);

  wire carry_la_1_p5, carry_la_2_p5, carry_la_3_p5, carry_la_4_p5, carry_la_5_p5;

  // Carry_LA carry_la_1: pin names not known; wires that end beside it: 1'b0, A[3:0], B[3:0], S[3:0], carry_la_1_p5
  // Carry_LA carry_la_2: pin names not known; wires that end beside it: carry_la_1_p5, A[7:4], B[7:4], S[7:4], carry_la_2_p5
  // Carry_LA carry_la_3: pin names not known; wires that end beside it: carry_la_2_p5, A[11:8], B[11:8], S[11:8], carry_la_3_p5
  // Carry_LA carry_la_4: pin names not known; wires that end beside it: carry_la_3_p5, A[15:12], B[15:12], S[15:12], carry_la_4_p5
  // Carry_LA carry_la_5: pin names not known; wires that end beside it: carry_la_4_p5, A[19:16], B[19:16], S[19:16], carry_la_5_p5
  // Carry_LA carry_la_6: pin names not known; wires that end beside it: carry_la_5_p5, A[23:20], B[23:20], S[23:20]

  // Other names for the same wires on the sheet: a0[3:0] = A[3:0]; a1[3:0] = A[7:4]; a2[3:0] = A[11:8];
  //   a3[3:0] = A[15:12]; a4[3:0] = A[19:16]; a5[3:0] = A[23:20]; b0[3:0] = B[3:0]; b1[3:0] = B[7:4];
  //   b2[3:0] = B[11:8]; b3[3:0] = B[15:12]; b4[3:0] = B[19:16]; b5[3:0] = B[23:20]
endmodule
