// Digital circuit mardo.dig as structural Verilog
module mardo (
  input  clk,
  input  clk_2
);

  wire add_1_c_o, branch_1_s, E, IP, Mux_ula, notconnected_1_out, notconnected_2_out, notconnected_3_out,
       notconnected_4_out, notconnected_5_out, notconnected_6_out, notconnected_7_out, notconnected_8_out,
       WE, zero;
  wire [2:0] ULA;
  wire [3:0] opencode_1_a, opencode_1_b, opencode_1_c, opencode_1_op;
  wire [15:0] opencode_1_const;
  wire [23:0] add_1_s, ip_1_s, multiplexer_1_out, signedextesion24bits_1_s;
  wire [31:0] and_1_out, bitextender_1_out, \Memória_de_Programa_d , multiplexer_2_out, registrador_1_a_2,
       registrador_1_b_2, ula_1_s, unsignedextension_1_p2;

  SignedExtesion24bits signedextesion24bits_1 (.\const (opencode_1_const), .S(signedextesion24bits_1_s));
  Multiplexer #(.Bits(24)) multiplexer_1 (
    .sel(branch_1_s), .in_0(24'h1), .in_1(signedextesion24bits_1_s), .out(multiplexer_1_out));
  IP ip_1 (.A(add_1_s), .Clock(clk), .S(ip_1_s));
  Branch branch_1 (.zero(zero), .IP(IP), .WE(WE), .S(branch_1_s));
  Add #(.Bits(24)) add_1 (.a(ip_1_s), .b(multiplexer_1_out), .c_i(1'b0), .s(add_1_s), .c_o(add_1_c_o));
  Seven_Seg_Hex seven_seg_hex_1 (.d(and_1_out[31:28]), .dp(notconnected_1_out));
  ROM #(.AddrBits(24), .Bits(32)) \Memória_de_Programa  (.A(ip_1_s), .sel(1'b1), .D(\Memória_de_Programa_d ));
  Seven_Seg_Hex seven_seg_hex_2 (.d(and_1_out[27:24]), .dp(notconnected_2_out));
  // NotConnected on notconnected_1_out
  // NotConnected on notconnected_2_out
  OpenCode opencode_1 (
    .in(\Memória_de_Programa_d ), .CONST(opencode_1_const), .C(opencode_1_c), .B(opencode_1_b),
    .A(opencode_1_a), .OP(opencode_1_op));
  Seven_Seg_Hex seven_seg_hex_3 (.d(and_1_out[23:20]), .dp(notconnected_3_out));
  // NotConnected on notconnected_3_out
  Seven_Seg_Hex seven_seg_hex_4 (.d(and_1_out[19:16]), .dp(notconnected_4_out));
  Seven_Seg_Hex seven_seg_hex_5 (.d(and_1_out[15:12]), .dp(notconnected_5_out));
  // NotConnected on notconnected_4_out
  BitExtender #(.inputBits(1), .outputBits(32)) bitextender_1 (.in(E), .out(bitextender_1_out));
  Registrador registrador_1 (
    .c(opencode_1_c), .WE(WE), .clock(clk_2), .b(opencode_1_b), .a(opencode_1_a), .C_2(ula_1_s),
    .A_2(registrador_1_a_2), .B_2(registrador_1_b_2));
  // unsignedExtension unsignedextension_1: pin names not known; wires that end beside it: opencode_1_const, unsignedextension_1_p2
  ROM #(.AddrBits(4), .Bits(7)) Memoria_de_Controle (.A(opencode_1_op), .sel(1'b1), .D({Mux_ula, ULA, WE, E, IP}));
  Seven_Seg_Hex seven_seg_hex_6 (.d(and_1_out[11:8]), .dp(notconnected_6_out));
  // NotConnected on notconnected_5_out
  // NotConnected on notconnected_6_out
  assign and_1_out = bitextender_1_out & registrador_1_a_2;  // And and_1, 32 bits wide
  Multiplexer #(.Bits(32)) multiplexer_2 (
    .sel(Mux_ula), .in_0(registrador_1_b_2), .in_1(unsignedextension_1_p2), .out(multiplexer_2_out));
  Seven_Seg_Hex seven_seg_hex_7 (.d(and_1_out[7:4]), .dp(notconnected_7_out));
  // NotConnected on notconnected_7_out
  ULA ula_1 (.A(registrador_1_a_2), .B(multiplexer_2_out), .sel(ULA), .S(ula_1_s), .zero(zero));
  Seven_Seg_Hex seven_seg_hex_8 (.d(and_1_out[3:0]), .dp(notconnected_8_out));
  // NotConnected on notconnected_8_out
  // also tied to GND on the sheet: add_1_c_o

  // Notes on the sheet:
  //   contents of Memória_de_Programa (hex, n*v repeats v):
  //   0,b2310003,c1000000,b2320006,c2000000,12130000,c3000000,22140000
  //   ,c4000000,34150000,44160000,54170000,62080000,72490000,c9000000
  //   ,824a0000,ca000000,920b0003,a20c0003,b20d0002,cd000000,c2000000
  //   ,d0000001,e55e0001,f0000000
  //   contents of Memoria_de_Controle (hex, n*v repeats v):
  //   0,4,c,14,1c,24,2c,34,3c,5c,64,44,2,1,d,41
endmodule
