// Digital circuit sl.dig as structural Verilog
module sl (
  input  [31:0] A,
  input  [31:0] B,
  output [31:0] S
);

  wire or_1_out;
  wire [31:0] shftleft_1bits_1_s, shftleft_2bits_1_s, shftleft_4bits_1_s, shftleft_8bits_1_s,
       shftleft_16bits_1_s;

  shftLeft_1bits shftleft_1bits_1 (.A(A), .B(B[0]), .S(shftleft_1bits_1_s));
  shftLeft_2bits shftleft_2bits_1 (.A(shftleft_1bits_1_s), .B(B[1]), .S(shftleft_2bits_1_s));
  or or_1 (or_1_out, B[5], B[6], B[7], B[8], B[9], B[10], B[11], B[12], B[13], B[14], B[15], B[16], B[17], B[18], B[19], B[20], B[21], B[22], B[23], B[24], B[25], B[26], B[27], B[28], B[29], B[30], B[31]);
  shftLeft_4bits shftleft_4bits_1 (.A(shftleft_2bits_1_s), .B(B[2]), .S(shftleft_4bits_1_s));
  shftLeft_8bits shftleft_8bits_1 (.A(shftleft_4bits_1_s), .B(B[3]), .S(shftleft_8bits_1_s));
  shftLeft_16bits shftleft_16bits_1 (.A(shftleft_8bits_1_s), .B(B[4]), .S(shftleft_16bits_1_s));
  Multiplexer #(.Bits(32)) multiplexer_1 (.sel(or_1_out), .in_0(shftleft_16bits_1_s), .in_1({32{1'b0}}), .out(S));
endmodule
